# Fritzing sketch 4_Ultrasonic_DHT11 (saved by Fritzing 0.9.4)
breadboards: 2

parts:
  YwRobot_Power_Supply1 = YwRobot Breadboard Power Supply [part_number=545043]
  M1 = DOIT Esp32 DevKit v1 (30 pins long, 11 pins width) [part_number=ESP32S-PIN30]
  HC-SR04_Sensor_1 = HC-SR04 Ultrasonic Distance Sensor
  DHT11_1 = DHT11 module

nets:
  VIN: YwRobot_Power_Supply1.VCC#5, YwRobot_Power_Supply1.VCC#6, M1.VIN, HC-SR04_Sensor_1.VCC, DHT11_1.DATA
  N1: YwRobot_Power_Supply1.VCC#9, YwRobot_Power_Supply1.VCC#10
  GND: YwRobot_Power_Supply1.GND#11, YwRobot_Power_Supply1.GND#12, M1.GND, HC-SR04_Sensor_1.GND, DHT11_1.GND
  N2: YwRobot_Power_Supply1.GND#13, YwRobot_Power_Supply1.GND#14
  N3: M1.D22, HC-SR04_Sensor_1.TRIG
  N4: M1.D23, HC-SR04_Sensor_1.ECHO
  N5: M1.D32, DHT11_1.VCC

custom parts:
  YwRobot Breadboard Power Supply: The YwRobot Breadboard Power Supply (MB-V2) has two power rails; they can be 5V or 3V3. Power to the module can be provided through the female USB socket or through the A10 (female) 2.1mm power jack.
  DOIT Esp32 DevKit v1 (30 pins long, 11 pins width): The DOIT Esp32 DevKit v1 is one of the development board created by DOIT to evaluate the ESP-WROOM-32 module. It is based on the ESP32 microcontroller that boasts Wifi, Bluetooth, Ethernet and Low Power support all in a single chip. (vanepp) made breadboard work, adjusted pin numbering and labels and reduced size of schematic and cleaned up pcb. This chip is 30pins long (2 x15) and 11 pins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
  DHT11 module: DHT11 black pcb module

// code stored in the sketch: 0_Print_IP_Address.ino
#include "ESP8266WiFi.h"

// WiFi parameters to be configured
const char* ssid = "Mi_WiFi";
const char* password = "MY_Password";

void setup(void)
{ 
  Serial.begin(9600);
  // Connect to WiFi
  WiFi.begin(ssid, password);

  // while wifi not connected yet, print '.'
  // then after it connected, get out of the loop
  while (WiFi.status() != WL_CONNECTED) {
     delay(500);
     Serial.print(".");
  }
  //print a new line, then print WiFi connected and the IP address
  Serial.println("");
  Serial.println("WiFi connected");
  // Print the IP address
  Serial.println(WiFi.localIP());

}
void loop() {
  // Nothing
}
