# Fritzing sketch 10 LDRs (saved by Fritzing 0.9.4)
breadboards: 1

parts:
  R1 = Photocell (LDR) [package=THT]
  R2 = Photocell (LDR) [package=THT]
  R3 = Photocell (LDR) [package=THT]
  R4 = Photocell (LDR) [package=THT]
  R5 = Photocell (LDR) [package=THT]
  R6 = Photocell (LDR) [package=THT]
  R7 = Photocell (LDR) [package=THT]
  R8 = Photocell (LDR) [package=THT]
  R9 = Photocell (LDR) [package=THT]
  R10 = Photocell (LDR) [package=THT]
  R11 = Resistor [tolerance=±5% resistance=220 package=THT]

nets:
  N1: R1.pin_1, R2.pin_0
  N2: R2.pin_1, R3.pin_0
  N3: R3.pin_1, R4.pin_0
  N4: R4.pin_1, R5.pin_0
  N5: R5.pin_1, R6.pin_0
  N6: R6.pin_1, R7.pin_0
  N7: R7.pin_1, R8.pin_0
  N8: R8.pin_1, R9.pin_0
  N9: R9.pin_1, R10.pin_0
  N10: R10.pin_1, R11.Pin_0
